// Logisim project LAB.circ as structural Verilog: 1 circuit, main circuit exp_3
module exp_3 (
  input  A,
  input  B,
  input  C,
  output I1,
  output F,
  output I2,
  output I3
);

  wire not_1_out, not_2_out;

  not not_1 (not_1_out, A);
  not not_2 (not_2_out, B);
  and AND (I1, not_1_out, C);
  and AND_2 (I2, A, not_2_out);
  and AND_3 (I3, B, C);
  or OR (F, I1, I2, I3);
endmodule
