// Logisim project Masruf_Jaman_1813625642.circ as structural Verilog: 11 circuits, main circuit exp1
module exp1 (
  input  B,
  input  F,
  input  J,
  input  C,
  input  G,
  input  K,
  input  D,
  input  H,
  input  A,
  input  E,
  input  I,
  input  L,
  input  M,
  output BCO,
  output FGO,
  output JKO,
  output DEO,
  output HIO,
  output AO,
  output LMO
);

  and AND (BCO, B, C);
  or OR (DEO, D, E);
  nand NAND (FGO, F, G);
  nor NOR (HIO, H, I);
  xnor XNOR (LMO, L, M);
  xor XOR (JKO, J, K);
  not NOT (AO, A);
endmodule

module exp2 (
  input  A,
  input  G,
  input  B,
  input  H,
  input  C,
  input  I,
  output F,
  output J
);

  wire AND_out, OR_out;

  and AND (AND_out, A, B);
  and AND_2 (F, AND_out, C);
  or OR (OR_out, G, H);
  or OR_2 (J, OR_out, I);
endmodule

module IC_7400 (
  input  in_1,
  input  in_2,
  input  in_3,
  input  in_4,
  input  in_5,
  input  in_6,
  input  in_7,
  input  in_8,
  input  in_9,
  input  in_10,
  output out_11,
  output out_12,
  output out_13,
  output out_14
);

  nand nand_1 (out_11, in_2, in_3);
  nand nand_2 (out_12, in_4, in_5);
  nand nand_3 (out_13, in_6, in_7);
  nand nand_4 (out_14, in_8, in_9);

  // Notes on the sheet:
  //   IC 7400 NAND
endmodule

module IC_7404 (
  input  in_1,
  input  in_2,
  input  in_3,
  input  in_4,
  input  in_5,
  input  in_6,
  input  in_7,
  input  in_8,
  output out_9,
  output out_10,
  output out_11,
  output out_12,
  output out_13,
  output out_14
);

  not not_1 (out_9, in_2);
  not not_2 (out_10, in_3);
  not not_3 (out_11, in_4);
  not not_4 (out_12, in_5);
  not not_5 (out_13, in_6);
  not not_6 (out_14, in_7);

  // Notes on the sheet:
  //   IC 7404 NOT
endmodule

module IC_7402 (
  input  in_1,
  input  in_2,
  input  in_3,
  input  in_4,
  input  in_5,
  input  in_6,
  input  in_7,
  input  in_8,
  input  in_9,
  input  in_10,
  output out_11,
  output out_12,
  output out_13,
  output out_14
);

  nor nor_1 (out_11, in_2, in_3);
  nor nor_2 (out_12, in_4, in_5);
  nor nor_3 (out_13, in_6, in_7);
  nor nor_4 (out_14, in_8, in_9);

  // Notes on the sheet:
  //   IC 7402 NOR
endmodule

module IC_7408 (
  input  in_1,
  input  in_2,
  input  in_3,
  input  in_4,
  input  in_5,
  input  in_6,
  input  in_7,
  input  in_8,
  input  in_9,
  input  in_10,
  output out_11,
  output out_12,
  output out_13,
  output out_14
);

  and and_1 (out_11, in_2, in_3);
  and and_2 (out_12, in_4, in_5);
  and and_3 (out_13, in_6, in_7);
  and and_4 (out_14, in_8, in_9);

  // Notes on the sheet:
  //   IC 7408 AND
endmodule

module test (
  input  in_1,
  input  in_2,
  input  in_3,
  input  in_4,
  input  in_5,
  input  in_6,
  input  in_7,
  input  in_8,
  input  in_9,
  input  in_10,
  input  in_11,
  output out_12,
  output out_13,
  output out_14,
  output out_15,
  output out_16,
  output out_17
);

  IC_7400 ic_7400_1 (
    .in_2(in_1), .in_3(in_4), .out_11(out_12));  // open: in_1, in_4, in_5, in_6, in_7, in_8, in_9, in_10, out_12, out_13, out_14
  IC_7404 ic_7404_1 (
    .in_2(in_7), .out_9(out_16));  // open: in_1, in_3, in_4, in_5, in_6, in_7, in_8, out_10, out_11, out_12, out_13, out_14
  IC_7408 ic_7408_1 (
    .in_2(in_2), .in_3(in_5), .out_11(out_13));  // open: in_1, in_4, in_5, in_6, in_7, in_8, in_9, in_10, out_12, out_13, out_14
  IC_7402 ic_7402_1 (
    .out_11(out_15), .in_2(in_9), .in_3(in_11));  // open: in_1, out_12, out_13, out_14, in_10, in_4, in_5, in_6, in_7, in_8, in_9
  IC_7432 ic_7432_1 (
    .in_2(in_3), .in_3(in_6), .out_11(out_14));  // open: in_1, in_4, in_5, in_6, in_7, in_8, in_9, in_10, out_12, out_13, out_14
  IC_7486 ic_7486_1 (
    .in_2(in_8), .in_3(in_10), .out_11(out_17));  // open: in_1, in_4, in_5, in_6, in_7, in_8, in_9, in_10, out_12, out_13, out_14

  // Notes on the sheet:
  //   NAND
  //   NOT
  //   AND
  //   NOR
  //   OR
  //   XOR
endmodule

module exp2_simulation (
  input  A,
  input  B,
  input  C,
  input  D,
  input  E,
  input  F,
  output Z
);

  wire AND_2_out, AND_3_out, AND_4_out, AND_out;

  and AND (AND_out, A, B);
  and AND_2 (AND_2_out, C, D);
  and AND_3 (AND_3_out, E, F);
  and AND_4 (AND_4_out, AND_out, AND_2_out);
  and AND_5 (Z, AND_4_out, AND_3_out);
endmodule

module IC_7432 (
  input  in_1,
  input  in_2,
  input  in_3,
  input  in_4,
  input  in_5,
  input  in_6,
  input  in_7,
  input  in_8,
  input  in_9,
  input  in_10,
  output out_11,
  output out_12,
  output out_13,
  output out_14
);

  or or_1 (out_11, in_2, in_3);
  or or_2 (out_12, in_4, in_5);
  or or_3 (out_13, in_6, in_7);
  or or_4 (out_14, in_8, in_9);

  // Notes on the sheet:
  //   IC 7432 OR
endmodule

module IC_7486 (
  input  in_1,
  input  in_2,
  input  in_3,
  input  in_4,
  input  in_5,
  input  in_6,
  input  in_7,
  input  in_8,
  input  in_9,
  input  in_10,
  output out_11,
  output out_12,
  output out_13,
  output out_14
);

  xor xor_1 (out_11, in_2, in_3);
  xor xor_2 (out_12, in_4, in_5);
  xor xor_3 (out_13, in_6, in_7);
  xor xor_4 (out_14, in_8, in_9);

  // Notes on the sheet:
  //   IC 7486 XOR
endmodule

module exp3 (
  input  A,
  input  B,
  input  C,
  output F
);

  wire A_prime_out, AND_2_out, AND_3_out, AND_out, B_prime_out, C_prime_out, OR_out;

  not A_prime (A_prime_out, A);
  not B_prime (B_prime_out, B);
  not C_prime (C_prime_out, C);
  and AND (AND_out, A_prime_out, C);
  and AND_2 (AND_2_out, A, B_prime_out);
  and AND_3 (AND_3_out, B, C);
  or OR (OR_out, AND_out, AND_2_out);
  or OR_2 (F, OR_out, AND_3_out);

  // Notes on the sheet:
  //   I1
  //   I2
  //   I3
endmodule
