// Logisim project Masruf_Jaman_1813625642_Lab_01_Exp_03.circ as structural Verilog: 7 circuits, main circuit IC 7400
module IC_7400 (
  input  in_1,
  input  in_2,
  input  in_3,
  input  in_4,
  input  in_5,
  input  in_6,
  input  in_7,
  input  in_8,
  input  in_9,
  input  in_10,
  output out_11,
  output out_12,
  output out_13,
  output out_14
);

  nand nand_1 (out_11, in_2, in_3);
  nand nand_2 (out_12, in_4, in_5);
  nand nand_3 (out_13, in_6, in_7);
  nand nand_4 (out_14, in_8, in_9);

  // Notes on the sheet:
  //   IC 7400 NAND
endmodule

module IC_7404 (
  input  in_1,
  input  in_2,
  input  in_3,
  input  in_4,
  input  in_5,
  input  in_6,
  input  in_7,
  input  in_8,
  output out_9,
  output out_10,
  output out_11,
  output out_12,
  output out_13,
  output out_14
);

  not not_1 (out_9, in_2);
  not not_2 (out_10, in_3);
  not not_3 (out_11, in_4);
  not not_4 (out_12, in_5);
  not not_5 (out_13, in_6);
  not not_6 (out_14, in_7);

  // Notes on the sheet:
  //   IC 7404 NOT
endmodule

module IC_7402 (
  input  in_1,
  input  in_2,
  input  in_3,
  input  in_4,
  input  in_5,
  input  in_6,
  input  in_7,
  input  in_8,
  input  in_9,
  input  in_10,
  output out_11,
  output out_12,
  output out_13,
  output out_14
);

  nor nor_1 (out_11, in_2, in_3);
  nor nor_2 (out_12, in_4, in_5);
  nor nor_3 (out_13, in_6, in_7);
  nor nor_4 (out_14, in_8, in_9);

  // Notes on the sheet:
  //   IC 7402 NOR
endmodule

module IC_7408 (
  input  in_1,
  input  in_2,
  input  in_3,
  input  in_4,
  input  in_5,
  input  in_6,
  input  in_7,
  input  in_8,
  input  in_9,
  input  in_10,
  output out_11,
  output out_12,
  output out_13,
  output out_14
);

  and and_1 (out_11, in_2, in_3);
  and and_2 (out_12, in_4, in_5);
  and and_3 (out_13, in_6, in_7);
  and and_4 (out_14, in_8, in_9);

  // Notes on the sheet:
  //   IC 7408 AND
endmodule

module IC_7432 (
  input  in_1,
  input  in_2,
  input  in_3,
  input  in_4,
  input  in_5,
  input  in_6,
  input  in_7,
  input  in_8,
  input  in_9,
  input  in_10,
  output out_11,
  output out_12,
  output out_13,
  output out_14
);

  or or_1 (out_11, in_2, in_3);
  or or_2 (out_12, in_4, in_5);
  or or_3 (out_13, in_6, in_7);
  or or_4 (out_14, in_8, in_9);

  // Notes on the sheet:
  //   IC 7432 OR
endmodule

module IC_7486 (
  input  in_1,
  input  in_2,
  input  in_3,
  input  in_4,
  input  in_5,
  input  in_6,
  input  in_7,
  input  in_8,
  input  in_9,
  input  in_10,
  output out_11,
  output out_12,
  output out_13,
  output out_14
);

  xor xor_1 (out_11, in_2, in_3);
  xor xor_2 (out_12, in_4, in_5);
  xor xor_3 (out_13, in_6, in_7);
  xor xor_4 (out_14, in_8, in_9);

  // Notes on the sheet:
  //   IC 7486 XOR
endmodule

module lab1_exp3 (
  input  A,
  input  B,
  input  C,
  output I1___A_prime_C,
  output I2___AB_prime,
  output F___A_prime_C___AB_prime___BC,
  output I3___BC
);

  wire ic_7404_1_out_9, ic_7404_1_out_10, ic_7432_1_out_11;

  IC_7408 ic_7408_1 (
    .in_2(ic_7404_1_out_9), .in_3(C), .in_4(A), .in_5(ic_7404_1_out_10), .in_6(C), .in_7(B),
    .out_11(I1___A_prime_C), .out_12(I2___AB_prime), .out_13(I3___BC));  // open: in_1, in_8, in_9, in_10, out_14
  IC_7404 ic_7404_1 (
    .in_2(A), .in_3(B), .out_9(ic_7404_1_out_9), .out_10(ic_7404_1_out_10));  // open: in_1, in_4, in_5, in_6, in_7, in_8, out_11, out_12, out_13, out_14
  IC_7432 ic_7432_1 (
    .in_2(I1___A_prime_C), .in_3(I2___AB_prime), .in_4(ic_7432_1_out_11), .in_5(I3___BC),
    .out_11(ic_7432_1_out_11), .out_12(F___A_prime_C___AB_prime___BC));  // open: in_1, in_6, in_7, in_8, in_9, in_10, out_13, out_14
endmodule
