// Logisim project Masruf_Jaman_1813625642.circ as structural Verilog: 4 circuits, main circuit universal_NOR_gate
module universal_NOR_gate (
  input  A,
  input  A_2,
  input  B,
  input  A_3,
  input  B_2,
  input  A_4,
  input  B_3,
  input  A_5,
  input  B_4,
  output F___A_prime,
  output F___AB,
  output F___A___B,
  output out_13,
  output out_14
);

  wire nor_2_out, nor_3_out, nor_4_out, nor_5_out, nor_6_out, nor_9_out, nor_10_out, nor_11_out, nor_12_out,
       nor_14_out;

  nor nor_1 (F___A_prime, A, A);
  nor nor_2 (nor_2_out, A_2, A_2);
  nor nor_3 (nor_3_out, B, B);
  nor nor_4 (nor_4_out, A_3, B_2);
  nor nor_5 (nor_5_out, A_4, B_3);
  nor nor_6 (nor_6_out, A_5, B_4);
  nor nor_7 (F___A___B, nor_4_out, nor_4_out);
  nor nor_8 (F___AB, nor_2_out, nor_3_out);
  nor nor_9 (nor_9_out, A_4, nor_5_out);
  nor nor_10 (nor_10_out, nor_5_out, B_3);
  nor nor_11 (nor_11_out, A_5, nor_6_out);
  nor nor_12 (nor_12_out, nor_6_out, B_4);
  nor nor_13 (out_13, nor_9_out, nor_10_out);
  nor nor_14 (nor_14_out, nor_11_out, nor_12_out);
  nor nor_15 (out_14, nor_14_out, nor_14_out);

  // Notes on the sheet:
  //   Universal NOR Gate
  //   implementation of NOT gate using NOR gate
  //   implementation of AND gate using NOR gate
  //   implementation of OR gate using NOR gate
  //   implementation of XNOR gate using NOR gate
  //   implementation of XOR gate using NOR gate
endmodule

module combinational_circuit_using_NAND (
  input  A,
  input  B,
  input  C,
  output F
);

  wire nand_1_out, nand_2_out, nand_3_out;

  nand nand_1 (nand_1_out, C, C);
  nand nand_2 (nand_2_out, A, C);
  nand nand_3 (nand_3_out, B, nand_1_out);
  nand nand_4 (F, nand_2_out, nand_3_out);
endmodule

module combinational_circuit_using_NOR (
  input  A,
  input  B,
  input  C,
  output F
);

  wire nor_1_out, nor_2_out, nor_3_out, nor_4_out, nor_5_out, nor_6_out, nor_7_out, nor_8_out;

  nor nor_1 (nor_1_out, A, A);
  nor nor_2 (nor_2_out, C, C);
  nor nor_3 (nor_3_out, B, B);
  nor nor_4 (nor_4_out, C, C);
  nor nor_5 (nor_5_out, nor_4_out, nor_4_out);
  nor nor_6 (nor_6_out, nor_1_out, nor_2_out);
  nor nor_7 (nor_7_out, nor_3_out, nor_5_out);
  nor nor_8 (nor_8_out, nor_6_out, nor_7_out);
  nor nor_9 (F, nor_8_out, nor_8_out);
endmodule

module universal_NAND_gate (
  input  A,
  input  A_2,
  input  B,
  input  A_3,
  input  B_2,
  input  A_4,
  input  B_3,
  input  A_5,
  input  B_4,
  output F___A_prime,
  output F___AB,
  output F___A___B,
  output F,
  output F_2
);

  wire nand_1_out, nand_3_out, nand_4_out, nand_5_out, nand_6_out, nand_9_out, nand_10_out, nand_11_out,
       nand_12_out, nand_14_out;

  nand nand_1 (nand_1_out, A_2, B);
  nand nand_2 (F___A_prime, A, A);
  nand nand_3 (nand_3_out, A_3, A_3);
  nand nand_4 (nand_4_out, B_2, B_2);
  nand nand_5 (nand_5_out, A_4, B_3);
  nand nand_6 (nand_6_out, A_5, B_4);
  nand nand_7 (F___AB, nand_1_out, nand_1_out);
  nand nand_8 (F___A___B, nand_3_out, nand_4_out);
  nand nand_9 (nand_9_out, A_4, nand_5_out);
  nand nand_10 (nand_10_out, nand_5_out, B_3);
  nand nand_11 (nand_11_out, A_5, nand_6_out);
  nand nand_12 (nand_12_out, nand_6_out, B_4);
  nand nand_13 (F, nand_9_out, nand_10_out);
  nand nand_14 (nand_14_out, nand_11_out, nand_12_out);
  nand nand_15 (F_2, nand_14_out, nand_14_out);

  // Notes on the sheet:
  //   Universal NAND Gate
  //   implementation of NOT gate using NAND gate
  //   implementation of AND gate using NAND gate
  //   implementation of OR gate using NAND gate
  //   implementation of XOR gate using NAND gate
  //   implementation of XNOR gate using NAND gate
endmodule
