// Logisim project Masruf_Jaman_1813625642.circ as structural Verilog: 11 circuits, main circuit IC 7400
module IC_7400 (
  input  in_1,
  input  in_2,
  input  in_3,
  input  in_4,
  input  in_5,
  input  in_6,
  input  in_7,
  input  in_8,
  input  in_9,
  input  in_10,
  output out_11,
  output out_12,
  output out_13,
  output out_14
);

  nand nand_1 (out_11, in_2, in_3);
  nand nand_2 (out_12, in_4, in_5);
  nand nand_3 (out_13, in_6, in_7);
  nand nand_4 (out_14, in_8, in_9);

  // Notes on the sheet:
  //   IC 7400 NAND
endmodule

module IC_7404 (
  input  in_1,
  input  in_2,
  input  in_3,
  input  in_4,
  input  in_5,
  input  in_6,
  input  in_7,
  input  in_8,
  output out_9,
  output out_10,
  output out_11,
  output out_12,
  output out_13,
  output out_14
);

  not not_1 (out_9, in_2);
  not not_2 (out_10, in_3);
  not not_3 (out_11, in_4);
  not not_4 (out_12, in_5);
  not not_5 (out_13, in_6);
  not not_6 (out_14, in_7);

  // Notes on the sheet:
  //   IC 7404 NOT
endmodule

module IC_7402 (
  input  in_1,
  input  in_2,
  input  in_3,
  input  in_4,
  input  in_5,
  input  in_6,
  input  in_7,
  input  in_8,
  input  in_9,
  input  in_10,
  output out_11,
  output out_12,
  output out_13,
  output out_14
);

  nor nor_1 (out_11, in_2, in_3);
  nor nor_2 (out_12, in_4, in_5);
  nor nor_3 (out_13, in_6, in_7);
  nor nor_4 (out_14, in_8, in_9);

  // Notes on the sheet:
  //   IC 7402 NOR
endmodule

module IC_7408 (
  input  in_1,
  input  in_2,
  input  in_3,
  input  in_4,
  input  in_5,
  input  in_6,
  input  in_7,
  input  in_8,
  input  in_9,
  input  in_10,
  output out_11,
  output out_12,
  output out_13,
  output out_14
);

  and and_1 (out_11, in_2, in_3);
  and and_2 (out_12, in_4, in_5);
  and and_3 (out_13, in_6, in_7);
  and and_4 (out_14, in_8, in_9);

  // Notes on the sheet:
  //   IC 7408 AND
endmodule

module IC_7432 (
  input  in_1,
  input  in_2,
  input  in_3,
  input  in_4,
  input  in_5,
  input  in_6,
  input  in_7,
  input  in_8,
  input  in_9,
  input  in_10,
  output out_11,
  output out_12,
  output out_13,
  output out_14
);

  or or_1 (out_11, in_2, in_3);
  or or_2 (out_12, in_4, in_5);
  or or_3 (out_13, in_6, in_7);
  or or_4 (out_14, in_8, in_9);

  // Notes on the sheet:
  //   IC 7432 OR
endmodule

module IC_7486 (
  input  in_1,
  input  in_2,
  input  in_3,
  input  in_4,
  input  in_5,
  input  in_6,
  input  in_7,
  input  in_8,
  input  in_9,
  input  in_10,
  output out_11,
  output out_12,
  output out_13,
  output out_14
);

  xor xor_1 (out_11, in_2, in_3);
  xor xor_2 (out_12, in_4, in_5);
  xor xor_3 (out_13, in_6, in_7);
  xor xor_4 (out_14, in_8, in_9);

  // Notes on the sheet:
  //   IC 7486 XOR
endmodule

module IC_4075 (
  input  A1,
  input  A2,
  input  A3,
  input  B1,
  input  B2,
  input  B3,
  input  C1,
  input  C2,
  input  C3,
  output AO,
  output BO,
  output CO
);

  or OR (AO, A1, A2, A3);
  or OR_2 (BO, B1, B2, B3);
  or OR_3 (CO, C1, C2, C3);

  // Notes on the sheet:
  //   3 INPUT OR GATE
endmodule

module IC_4073 (
  input  A1,
  input  A2,
  input  A3,
  input  B1,
  input  B2,
  input  B3,
  input  C1,
  input  C2,
  input  C3,
  output AO,
  output BO,
  output CO
);

  and AND (AO, A1, A2, A3);
  and AND_2 (BO, B1, B2, B3);
  and AND_3 (CO, C1, C2, C3);

  // Notes on the sheet:
  //   3 INPUT AND GATE
endmodule

module _1st_Canonical_form (
  input  A,
  input  B,
  input  C,
  output F
);

  wire ic_4073_1_ao, ic_4073_1_bo, ic_4073_1_co, ic_7404_1_out_9, ic_7404_1_out_10, ic_7404_1_out_11;

  IC_7404 ic_7404_1 (
    .in_2(A), .in_3(B), .in_4(C), .out_9(ic_7404_1_out_9), .out_10(ic_7404_1_out_10),
    .out_11(ic_7404_1_out_11));  // open: in_1, in_5, in_6, in_7, in_8, out_12, out_13, out_14
  IC_4073 ic_4073_1 (
    .A1(ic_7404_1_out_9), .A2(B), .A3(ic_7404_1_out_11), .B1(ic_7404_1_out_9), .B2(ic_7404_1_out_10), .B3(C),
    .C1(A), .C2(B), .C3(ic_7404_1_out_11), .AO(ic_4073_1_ao), .BO(ic_4073_1_bo), .CO(ic_4073_1_co));
  IC_4075 ic_4075_1 (
    .B1(ic_4073_1_co), .B2(ic_4073_1_ao), .B3(ic_4073_1_bo), .BO(F));  // open: A1, A2, A3, C1, C2, C3, AO, CO

  // Notes on the sheet:
  //   6 = A'.B'.C
  //   F = A'.B'.C + A'.B.C' + A.B.C'
  //   10 = A.B.C'
  //   9 = A'.B.C'
endmodule

module _2nd_Canonical_form (
  input  A,
  input  B,
  input  C,
  output F
);

  wire ic_4073_1_ao, ic_4075_1_ao, ic_4075_1_bo, ic_4075_1_co, ic_4075_2_bo, ic_4075_2_co, ic_7404_1_out_9,
       ic_7404_1_out_10, ic_7404_1_out_11;

  IC_7404 ic_7404_1 (
    .in_2(A), .in_3(B), .in_4(C), .out_9(ic_7404_1_out_9), .out_10(ic_7404_1_out_10),
    .out_11(ic_7404_1_out_11));  // open: in_1, in_5, in_6, in_7, in_8, out_12, out_13, out_14
  IC_4075 ic_4075_1 (
    .A1(A), .A2(ic_7404_1_out_10), .A3(ic_7404_1_out_11), .B1(ic_7404_1_out_9), .B2(B), .B3(C), .C1(C),
    .C2(B), .C3(C), .AO(ic_4075_1_ao), .BO(ic_4075_1_bo), .CO(ic_4075_1_co));
  IC_4075 ic_4075_2 (
    .B1(ic_7404_1_out_9), .B2(B), .B3(ic_7404_1_out_11), .C1(ic_7404_1_out_11), .C2(ic_7404_1_out_10),
    .C3(ic_7404_1_out_9), .BO(ic_4075_2_bo), .CO(ic_4075_2_co));  // open: A1, A2, A3, AO
  IC_4073 ic_4073_1 (
    .A1(ic_4075_1_ao), .A2(ic_4075_1_bo), .A3(ic_4075_1_co), .B1(ic_4075_2_co), .B2(ic_4075_2_bo),
    .B3(ic_4073_1_ao), .AO(ic_4073_1_ao), .BO(F));  // open: C1, C2, C3, CO

  // Notes on the sheet:
  //   6 = A' + B +C
  //   6 = A' + B +C'
  //   F = (A+B+C).(A+B'+C').(A'+B+C).(A'+B+C').(A'+B'+C')
  //   10 = A + B + C
  //   9 = A + B' + C'
  //   10 = A' + B' + C'
endmodule

module _2nd_canonical_form_using_gates (
  input  A,
  input  B,
  input  C,
  output F
);

  wire A_prime_out, AND_out, B_prime_out, C_prime_out, OR_2_out, OR_3_out, OR_4_out, OR_5_out, OR_out;

  not A_prime (A_prime_out, A);
  not B_prime (B_prime_out, B);
  not C_prime (C_prime_out, C);
  or OR (OR_out, A, B, C);
  or OR_2 (OR_2_out, A, B_prime_out, C_prime_out);
  or OR_3 (OR_3_out, A_prime_out, B, C);
  or OR_4 (OR_4_out, A_prime_out, B, C_prime_out);
  or OR_5 (OR_5_out, A_prime_out, B_prime_out, C_prime_out);
  and AND (AND_out, OR_out, OR_2_out, OR_3_out);
  and AND_2 (F, AND_out, OR_4_out, OR_5_out);

  // Notes on the sheet:
  //   F = (A+B+C).(A+B'+C').(A'+B+C).(A'+B+C').(A'+B'+C')
  //   A+B+C
  //   A+B'+C'
  //   A'+B+C
  //   A'+B+C'
  //   A'+B'+C'
  //   (A+B+C).(A+B'+C').(A'+B+C)
  //   (A+B+C).(A+B'+C').(A'+B+C).(A'+B+C').(A'+B'+C')
endmodule
