// Logisim project Masruf_Jaman_1813625642.circ as structural Verilog: 11 circuits, main circuit IC 7404
module IC_7400 (
  input  in_1,
  input  in_2,
  input  in_3,
  input  in_4,
  input  in_5,
  input  in_6,
  input  in_7,
  input  in_8,
  input  in_9,
  input  in_10,
  output out_11,
  output out_12,
  output out_13,
  output out_14
);

  nand nand_1 (out_11, in_2, in_3);
  nand nand_2 (out_12, in_4, in_5);
  nand nand_3 (out_13, in_6, in_7);
  nand nand_4 (out_14, in_8, in_9);

  // Notes on the sheet:
  //   IC 7400 NAND
endmodule

module IC_7404 (
  input  in_1,
  input  in_2,
  input  in_3,
  input  in_4,
  input  in_5,
  input  in_6,
  input  in_7,
  input  in_8,
  output out_9,
  output out_10,
  output out_11,
  output out_12,
  output out_13,
  output out_14
);

  not not_1 (out_9, in_2);
  not not_2 (out_10, in_3);
  not not_3 (out_11, in_4);
  not not_4 (out_12, in_5);
  not not_5 (out_13, in_6);
  not not_6 (out_14, in_7);

  // Notes on the sheet:
  //   IC 7404 NOT
endmodule

module IC_7402 (
  input  in_1,
  input  in_2,
  input  in_3,
  input  in_4,
  input  in_5,
  input  in_6,
  input  in_7,
  input  in_8,
  input  in_9,
  input  in_10,
  output out_11,
  output out_12,
  output out_13,
  output out_14
);

  nor nor_1 (out_11, in_2, in_3);
  nor nor_2 (out_12, in_4, in_5);
  nor nor_3 (out_13, in_6, in_7);
  nor nor_4 (out_14, in_8, in_9);

  // Notes on the sheet:
  //   IC 7402 NOR
endmodule

module IC_7408 (
  input  in_1,
  input  in_2,
  input  in_3,
  input  in_4,
  input  in_5,
  input  in_6,
  input  in_7,
  input  in_8,
  input  in_9,
  input  in_10,
  output out_11,
  output out_12,
  output out_13,
  output out_14
);

  and and_1 (out_11, in_2, in_3);
  and and_2 (out_12, in_4, in_5);
  and and_3 (out_13, in_6, in_7);
  and and_4 (out_14, in_8, in_9);

  // Notes on the sheet:
  //   IC 7408 AND
endmodule

module IC_7432 (
  input  in_1,
  input  in_2,
  input  in_3,
  input  in_4,
  input  in_5,
  input  in_6,
  input  in_7,
  input  in_8,
  input  in_9,
  input  in_10,
  output out_11,
  output out_12,
  output out_13,
  output out_14
);

  or or_1 (out_11, in_2, in_3);
  or or_2 (out_12, in_4, in_5);
  or or_3 (out_13, in_6, in_7);
  or or_4 (out_14, in_8, in_9);

  // Notes on the sheet:
  //   IC 7432 OR
endmodule

module IC_7486 (
  input  in_1,
  input  in_2,
  input  in_3,
  input  in_4,
  input  in_5,
  input  in_6,
  input  in_7,
  input  in_8,
  input  in_9,
  input  in_10,
  output out_11,
  output out_12,
  output out_13,
  output out_14
);

  xor xor_1 (out_11, in_2, in_3);
  xor xor_2 (out_12, in_4, in_5);
  xor xor_3 (out_13, in_6, in_7);
  xor xor_4 (out_14, in_8, in_9);

  // Notes on the sheet:
  //   IC 7486 XOR
endmodule

module IC_4075 (
  input  A1,
  input  A2,
  input  A3,
  input  B1,
  input  B2,
  input  B3,
  input  C1,
  input  C2,
  input  C3,
  output AO,
  output BO,
  output CO
);

  or OR (AO, A1, A2, A3);
  or OR_2 (BO, B1, B2, B3);
  or OR_3 (CO, C1, C2, C3);

  // Notes on the sheet:
  //   3 INPUT OR GATE
endmodule

module IC_4073 (
  input  A1,
  input  A2,
  input  A3,
  input  B1,
  input  B2,
  input  B3,
  input  C1,
  input  C2,
  input  C3,
  output AO,
  output BO,
  output CO
);

  and AND (AO, A1, A2, A3);
  and AND_2 (BO, B1, B2, B3);
  and AND_3 (CO, C1, C2, C3);

  // Notes on the sheet:
  //   3 INPUT AND GATE
endmodule

module Task_01 (
  input  W,
  input  X,
  input  Y,
  input  Z,
  output A___W___XY___XZ,
  output B___X_prime_Y___X_prime_Z___XY_prime_Z_prime,
  output C___YZ___Y_prime_Z_prime,
  output D___Z_prime
);

  wire and_1_out, and_2_out, and_3_out, and_4_out, and_5_out, and_6_out, and_7_out, X_prime_out, Y_prime_out;

  not X_prime (X_prime_out, X);
  not Z_prime (D___Z_prime, Z);
  not Y_prime (Y_prime_out, Y);
  and and_1 (and_1_out, X, Y);
  and and_2 (and_2_out, X, Z);
  and and_3 (and_3_out, X_prime_out, Y);
  and and_4 (and_4_out, X_prime_out, Z);
  and and_5 (and_5_out, X, Y_prime_out, D___Z_prime);
  and and_6 (and_6_out, Y, Z);
  and and_7 (and_7_out, Y_prime_out, D___Z_prime);
  or or_1 (A___W___XY___XZ, W, and_1_out, and_2_out);
  or or_2 (B___X_prime_Y___X_prime_Z___XY_prime_Z_prime, and_3_out, and_4_out, and_5_out);
  or or_3 (C___YZ___Y_prime_Z_prime, and_6_out, and_7_out);

  // Notes on the sheet:
  //   XY
  //   XZ
  //   X'Y
  //   X'Z
  //   XY'Z'
  //   Y'Z'
  //   YZ
endmodule

module Task_02 (
  input  W,
  input  X,
  input  Y,
  input  Z,
  output A,
  output B,
  output C,
  output D
);

  wire ic_4073_1_bo, ic_7404_1_out_9, ic_7404_1_out_10, ic_7408_1_out_11, ic_7408_1_out_12, ic_7408_1_out_13,
       ic_7408_1_out_14, ic_7408_2_out_11, ic_7408_2_out_12;

  IC_7404 ic_7404_1 (
    .in_2(X), .in_3(Y), .in_4(Z), .out_9(ic_7404_1_out_9), .out_10(ic_7404_1_out_10), .out_11(D));  // open: in_1, in_5, in_6, in_7, in_8, out_12, out_13, out_14
  IC_7408 ic_7408_1 (
    .in_2(X), .in_3(Y), .in_4(X), .in_5(Z), .in_6(Z), .in_7(ic_7404_1_out_9), .in_8(Y),
    .in_9(ic_7404_1_out_9), .out_11(ic_7408_1_out_11), .out_12(ic_7408_1_out_12), .out_13(ic_7408_1_out_13),
    .out_14(ic_7408_1_out_14));  // open: in_1, in_10
  IC_7408 ic_7408_2 (
    .in_2(Y), .in_3(Z), .in_4(ic_7404_1_out_10), .in_5(D), .out_11(ic_7408_2_out_11),
    .out_12(ic_7408_2_out_12));  // open: in_1, in_6, in_7, in_8, in_9, in_10, out_13, out_14
  IC_4073 ic_4073_1 (.B1(X), .B2(ic_7404_1_out_10), .B3(D), .BO(ic_4073_1_bo));  // open: A1, A2, A3, C1, C2, C3, AO, CO
  IC_4075 ic_4075_1 (
    .A1(ic_7408_1_out_11), .A2(ic_7408_1_out_12), .A3(W), .B1(ic_7408_1_out_14), .B2(ic_7408_1_out_13),
    .B3(ic_4073_1_bo), .AO(A), .BO(B));  // open: C1, C2, C3, CO
  IC_7432 ic_7432_1 (
    .in_2(ic_7408_2_out_11), .in_3(ic_7408_2_out_12), .out_11(C));  // open: in_1, in_4, in_5, in_6, in_7, in_8, in_9, in_10, out_12, out_13, out_14
endmodule

module Figure_F2 (
  input  W,
  input  X,
  input  Y,
  input  Z,
  output A___W___XY___XZ,
  output B___X_prime_Y___X_prime_Z___XY_prime_Z_prime,
  output C___YZ___Y_prime_Z_prime,
  output D___Z_prime
);

  wire nand_1_out, nand_2_out, nand_4_out, nand_5_out, nand_6_out, nand_7_out, nand_8_out, nand_9_out,
       nand_10_out, nand_11_out;

  nand nand_1 (nand_1_out, X, X);
  nand nand_2 (nand_2_out, Y, Y);
  nand nand_3 (D___Z_prime, Z, Z);
  nand nand_4 (nand_4_out, X, Y);
  nand nand_5 (nand_5_out, X, Z);
  nand nand_6 (nand_6_out, nand_1_out, Y);
  nand nand_7 (nand_7_out, nand_1_out, Z);
  nand nand_8 (nand_8_out, X, nand_2_out, D___Z_prime);
  nand nand_9 (nand_9_out, Y, Z);
  nand nand_10 (nand_10_out, nand_2_out, D___Z_prime);
  nand nand_11 (nand_11_out, W, W);
  nand nand_12 (A___W___XY___XZ, nand_11_out, nand_4_out, nand_5_out);
  nand nand_13 (B___X_prime_Y___X_prime_Z___XY_prime_Z_prime, nand_6_out, nand_7_out, nand_8_out);
  nand nand_14 (C___YZ___Y_prime_Z_prime, nand_9_out, nand_10_out);
endmodule
