// Logisim project Masruf_Jaman_1813625642.circ as structural Verilog: 12 circuits, main circuit IC 7404
module IC_7400 (
  input  in_1,
  input  in_2,
  input  in_3,
  input  in_4,
  input  in_5,
  input  in_6,
  input  in_7,
  input  in_8,
  input  in_9,
  input  in_10,
  output out_11,
  output out_12,
  output out_13,
  output out_14
);

  nand nand_1 (out_11, in_2, in_3);
  nand nand_2 (out_12, in_4, in_5);
  nand nand_3 (out_13, in_6, in_7);
  nand nand_4 (out_14, in_8, in_9);

  // Notes on the sheet:
  //   IC 7400 NAND
endmodule

module IC_7404 (
  input  in_1,
  input  in_2,
  input  in_3,
  input  in_4,
  input  in_5,
  input  in_6,
  input  in_7,
  input  in_8,
  output out_9,
  output out_10,
  output out_11,
  output out_12,
  output out_13,
  output out_14
);

  not not_1 (out_9, in_2);
  not not_2 (out_10, in_3);
  not not_3 (out_11, in_4);
  not not_4 (out_12, in_5);
  not not_5 (out_13, in_6);
  not not_6 (out_14, in_7);

  // Notes on the sheet:
  //   IC 7404 NOT
endmodule

module IC_7402 (
  input  in_1,
  input  in_2,
  input  in_3,
  input  in_4,
  input  in_5,
  input  in_6,
  input  in_7,
  input  in_8,
  input  in_9,
  input  in_10,
  output out_11,
  output out_12,
  output out_13,
  output out_14
);

  nor nor_1 (out_11, in_2, in_3);
  nor nor_2 (out_12, in_4, in_5);
  nor nor_3 (out_13, in_6, in_7);
  nor nor_4 (out_14, in_8, in_9);

  // Notes on the sheet:
  //   IC 7402 NOR
endmodule

module IC_7408 (
  input  in_1,
  input  in_2,
  input  in_3,
  input  in_4,
  input  in_5,
  input  in_6,
  input  in_7,
  input  in_8,
  input  in_9,
  input  in_10,
  output out_11,
  output out_12,
  output out_13,
  output out_14
);

  and and_1 (out_11, in_2, in_3);
  and and_2 (out_12, in_4, in_5);
  and and_3 (out_13, in_6, in_7);
  and and_4 (out_14, in_8, in_9);

  // Notes on the sheet:
  //   IC 7408 AND
endmodule

module IC_7432 (
  input  in_1,
  input  in_2,
  input  in_3,
  input  in_4,
  input  in_5,
  input  in_6,
  input  in_7,
  input  in_8,
  input  in_9,
  input  in_10,
  output out_11,
  output out_12,
  output out_13,
  output out_14
);

  or or_1 (out_11, in_2, in_3);
  or or_2 (out_12, in_4, in_5);
  or or_3 (out_13, in_6, in_7);
  or or_4 (out_14, in_8, in_9);

  // Notes on the sheet:
  //   IC 7432 OR
endmodule

module IC_7486 (
  input  in_1,
  input  in_2,
  input  in_3,
  input  in_4,
  input  in_5,
  input  in_6,
  input  in_7,
  input  in_8,
  input  in_9,
  input  in_10,
  output out_11,
  output out_12,
  output out_13,
  output out_14
);

  xor xor_1 (out_11, in_2, in_3);
  xor xor_2 (out_12, in_4, in_5);
  xor xor_3 (out_13, in_6, in_7);
  xor xor_4 (out_14, in_8, in_9);

  // Notes on the sheet:
  //   IC 7486 XOR
endmodule

module IC_4075 (
  input  A1,
  input  A2,
  input  A3,
  input  B1,
  input  B2,
  input  B3,
  input  C1,
  input  C2,
  input  C3,
  output AO,
  output BO,
  output CO
);

  or OR (AO, A1, A2, A3);
  or OR_2 (BO, B1, B2, B3);
  or OR_3 (CO, C1, C2, C3);

  // Notes on the sheet:
  //   3 INPUT OR GATE
endmodule

module IC_4073 (
  input  A1,
  input  A2,
  input  A3,
  input  B1,
  input  B2,
  input  B3,
  input  C1,
  input  C2,
  input  C3,
  output AO,
  output BO,
  output CO
);

  and AND (AO, A1, A2, A3);
  and AND_2 (BO, B1, B2, B3);
  and AND_3 (CO, C1, C2, C3);

  // Notes on the sheet:
  //   3 INPUT AND GATE
endmodule

module IC_7483 (
  input  GND,
  input  VCC,
  input  C_in,
  input  A4,
  input  A3,
  input  A2,
  input  A1,
  input  B4,
  input  B3,
  input  B2,
  input  B1,
  output C_out,
  output S4,
  output S3,
  output S2,
  output S1
);

  wire and_1_out, and_2_out, and_3_out, and_4_out, and_5_out, and_6_out, and_7_out, and_8_out, or_1_out,
       or_2_out, or_3_out, xor_1_out, xor_2_out, xor_3_out, xor_4_out;

  xor xor_1 (xor_1_out, B1, A1);
  and and_1 (and_1_out, B1, A1);
  xor xor_2 (xor_2_out, B2, A2);
  and and_2 (and_2_out, B2, A2);
  xor xor_3 (xor_3_out, B3, A3);
  and and_3 (and_3_out, B3, A3);
  and and_4 (and_4_out, B4, A4);
  xor xor_4 (xor_4_out, B4, A4);
  and and_5 (and_5_out, xor_1_out, C_in);
  and and_6 (and_6_out, xor_2_out, or_1_out);
  xor xor_5 (S1, xor_1_out, C_in);
  xor xor_6 (S2, xor_2_out, or_1_out);
  xor xor_7 (S3, xor_3_out, or_2_out);
  and and_7 (and_7_out, xor_3_out, or_2_out);
  xor xor_8 (S4, xor_4_out, or_3_out);
  and and_8 (and_8_out, xor_4_out, or_3_out);
  or or_1 (or_1_out, and_5_out, and_1_out);
  or or_2 (or_2_out, and_6_out, and_2_out);
  or or_3 (or_3_out, and_7_out, and_3_out);
  or or_4 (C_out, and_8_out, and_4_out);
endmodule

module TASK_1 (
  input  A4,
  input  A3,
  input  A2,
  input  A1,
  input  B4,
  input  B3,
  input  B2,
  input  B1,
  input  MODE,
  output S4,
  output S3,
  output S2,
  output S1
);

  wire ic_7486_1_out_11, ic_7486_1_out_12, ic_7486_1_out_13, ic_7486_1_out_14;

  IC_7486 ic_7486_1 (
    .in_2(B4), .in_3(MODE), .in_4(B3), .in_5(MODE), .in_6(MODE), .in_7(B1), .in_8(MODE), .in_9(B2),
    .out_11(ic_7486_1_out_11), .out_12(ic_7486_1_out_12), .out_13(ic_7486_1_out_13), .out_14(ic_7486_1_out_14));  // open: in_1, in_10
  IC_7483 ic_7483_1 (
    .A4(A4), .A3(A3), .A2(A2), .A1(A1), .B4(ic_7486_1_out_11), .B3(ic_7486_1_out_12), .B2(ic_7486_1_out_14),
    .B1(ic_7486_1_out_13), .C_in(MODE), .S4(S4), .S3(S3), .S2(S2), .S1(S1));  // open: GND, VCC, C_out
endmodule

module TASK_3 (
  input  A4__A1,
  input  A4,
  input  A3,
  input  A2,
  input  A1,
  input  B4,
  input  B3,
  input  B2,
  input  C_in,
  input  B1,
  input  C_in_2,
  output out_12,
  output S4,
  output S3,
  output S2,
  output S1
);

  wire ic_7408_1_out_11, ic_7408_1_out_12, ic_7483_1_c_out, ic_7483_1_s1, ic_7483_1_s2, ic_7483_1_s3,
       ic_7483_1_s4;

  IC_7483 ic_7483_1 (
    .A4(A4), .A3(A3), .A2(A2), .A1(A1), .B4(B4), .B3(B3), .B2(B2), .B1(B1), .C_in(C_in_2),
    .C_out(ic_7483_1_c_out), .S4(ic_7483_1_s4), .S3(ic_7483_1_s3), .S2(ic_7483_1_s2), .S1(ic_7483_1_s1));  // open: GND, VCC
  IC_7483 ic_7483_2 (
    .GND(C_in), .A4(ic_7483_1_s4), .A3(ic_7483_1_s3), .A2(ic_7483_1_s2), .A1(ic_7483_1_s1), .B4(A4__A1),
    .B3(out_12), .B2(out_12), .B1(A4__A1), .C_in(C_in), .S4(S4), .S3(S3), .S2(S2), .S1(S1));  // open: VCC, C_out
  IC_7408 ic_7408_1 (
    .in_2(ic_7483_1_s4), .in_3(ic_7483_1_s3), .in_4(ic_7483_1_s4), .in_5(ic_7483_1_s2),
    .out_11(ic_7408_1_out_11), .out_12(ic_7408_1_out_12));  // open: in_1, in_6, in_7, in_8, in_9, in_10, out_13, out_14
  IC_4075 ic_4075_1 (
    .B1(ic_7483_1_c_out), .B2(ic_7408_1_out_11), .B3(ic_7408_1_out_12), .BO(out_12));  // open: A1, A2, A3, C1, C2, C3, AO, CO
endmodule

module Task_2 (
  input  A8,
  input  A7,
  input  A6,
  input  A5,
  input  A4,
  input  A3,
  input  A2,
  input  A1,
  input  B8,
  input  C_in,
  input  B7,
  input  B6,
  input  B5,
  input  B4,
  input  B3,
  input  B2,
  input  B1,
  output S8,
  output S7,
  output S6,
  output S5,
  output S4,
  output S3,
  output S2,
  output S1,
  output C_out
);

  wire ic_7483_1_c_out;

  IC_7483 ic_7483_1 (
    .A4(A8), .A3(A7), .A2(A6), .A1(A5), .B4(B8), .B3(B7), .B2(B6), .B1(B5), .C_in(C_in),
    .C_out(ic_7483_1_c_out), .S4(S8), .S3(S7), .S2(S6), .S1(S5));  // open: GND, VCC
  IC_7483 ic_7483_2 (
    .A4(A4), .A3(A3), .A2(A2), .A1(A1), .B4(B4), .B3(B3), .B2(B2), .B1(B1), .C_in(ic_7483_1_c_out),
    .C_out(C_out), .S4(S4), .S3(S3), .S2(S2), .S1(S1));  // open: GND, VCC
endmodule
