// Logisim project Lab-06_Masruf_Jaman_1813625642.circ as structural Verilog: 14 circuits, main circuit IC 7404
module IC_7400 (
  input  in_1,
  input  in_2,
  input  in_3,
  input  in_4,
  input  in_5,
  input  in_6,
  input  in_7,
  input  in_8,
  input  in_9,
  input  in_10,
  output out_11,
  output out_12,
  output out_13,
  output out_14
);

  nand nand_1 (out_11, in_2, in_3);
  nand nand_2 (out_12, in_4, in_5);
  nand nand_3 (out_13, in_6, in_7);
  nand nand_4 (out_14, in_8, in_9);

  // Notes on the sheet:
  //   IC 7400 NAND
endmodule

module IC_7404 (
  input  in_1,
  input  in_2,
  input  in_3,
  input  in_4,
  input  in_5,
  input  in_6,
  input  in_7,
  input  in_8,
  output out_9,
  output out_10,
  output out_11,
  output out_12,
  output out_13,
  output out_14
);

  not not_1 (out_9, in_2);
  not not_2 (out_10, in_3);
  not not_3 (out_11, in_4);
  not not_4 (out_12, in_5);
  not not_5 (out_13, in_6);
  not not_6 (out_14, in_7);

  // Notes on the sheet:
  //   IC 7404 NOT
endmodule

module IC_7402 (
  input  in_1,
  input  in_2,
  input  in_3,
  input  in_4,
  input  in_5,
  input  in_6,
  input  in_7,
  input  in_8,
  input  in_9,
  input  in_10,
  output out_11,
  output out_12,
  output out_13,
  output out_14
);

  nor nor_1 (out_11, in_2, in_3);
  nor nor_2 (out_12, in_4, in_5);
  nor nor_3 (out_13, in_6, in_7);
  nor nor_4 (out_14, in_8, in_9);

  // Notes on the sheet:
  //   IC 7402 NOR
endmodule

module IC_7408 (
  input  in_1,
  input  in_2,
  input  in_3,
  input  in_4,
  input  in_5,
  input  in_6,
  input  in_7,
  input  in_8,
  input  in_9,
  input  in_10,
  output out_11,
  output out_12,
  output out_13,
  output out_14
);

  and and_1 (out_11, in_2, in_3);
  and and_2 (out_12, in_4, in_5);
  and and_3 (out_13, in_6, in_7);
  and and_4 (out_14, in_8, in_9);

  // Notes on the sheet:
  //   IC 7408 AND
endmodule

module IC_7432 (
  input  in_1,
  input  in_2,
  input  in_3,
  input  in_4,
  input  in_5,
  input  in_6,
  input  in_7,
  input  in_8,
  input  in_9,
  input  in_10,
  output out_11,
  output out_12,
  output out_13,
  output out_14
);

  or or_1 (out_11, in_2, in_3);
  or or_2 (out_12, in_4, in_5);
  or or_3 (out_13, in_6, in_7);
  or or_4 (out_14, in_8, in_9);

  // Notes on the sheet:
  //   IC 7432 OR
endmodule

module IC_7486 (
  input  in_1,
  input  in_2,
  input  in_3,
  input  in_4,
  input  in_5,
  input  in_6,
  input  in_7,
  input  in_8,
  input  in_9,
  input  in_10,
  output out_11,
  output out_12,
  output out_13,
  output out_14
);

  xor xor_1 (out_11, in_2, in_3);
  xor xor_2 (out_12, in_4, in_5);
  xor xor_3 (out_13, in_6, in_7);
  xor xor_4 (out_14, in_8, in_9);

  // Notes on the sheet:
  //   IC 7486 XOR
endmodule

module IC_4075 (
  input  A1,
  input  A2,
  input  A3,
  input  B1,
  input  B2,
  input  B3,
  input  C1,
  input  C2,
  input  C3,
  output AO,
  output BO,
  output CO
);

  or OR (AO, A1, A2, A3);
  or OR_2 (BO, B1, B2, B3);
  or OR_3 (CO, C1, C2, C3);

  // Notes on the sheet:
  //   3 INPUT OR GATE
endmodule

module IC_4073 (
  input  A1,
  input  A2,
  input  A3,
  input  B1,
  input  B2,
  input  B3,
  input  C1,
  input  C2,
  input  C3,
  output AO,
  output BO,
  output CO
);

  and AND (AO, A1, A2, A3);
  and AND_2 (BO, B1, B2, B3);
  and AND_3 (CO, C1, C2, C3);

  // Notes on the sheet:
  //   3 INPUT AND GATE
endmodule

module IC_7483 (
  input  GND,
  input  VCC,
  input  C_in,
  input  A4,
  input  A3,
  input  A2,
  input  A1,
  input  B4,
  input  B3,
  input  B2,
  input  B1,
  output C_out,
  output S4,
  output S3,
  output S2,
  output S1
);

  wire and_1_out, and_2_out, and_3_out, and_4_out, and_5_out, and_6_out, and_7_out, and_8_out, or_1_out,
       or_2_out, or_3_out, xor_1_out, xor_2_out, xor_3_out, xor_4_out;

  xor xor_1 (xor_1_out, B1, A1);
  and and_1 (and_1_out, B1, A1);
  xor xor_2 (xor_2_out, B2, A2);
  and and_2 (and_2_out, B2, A2);
  xor xor_3 (xor_3_out, B3, A3);
  and and_3 (and_3_out, B3, A3);
  and and_4 (and_4_out, B4, A4);
  xor xor_4 (xor_4_out, B4, A4);
  and and_5 (and_5_out, xor_1_out, C_in);
  and and_6 (and_6_out, xor_2_out, or_1_out);
  xor xor_5 (S1, xor_1_out, C_in);
  xor xor_6 (S2, xor_2_out, or_1_out);
  xor xor_7 (S3, xor_3_out, or_2_out);
  and and_7 (and_7_out, xor_3_out, or_2_out);
  xor xor_8 (S4, xor_4_out, or_3_out);
  and and_8 (and_8_out, xor_4_out, or_3_out);
  or or_1 (or_1_out, and_5_out, and_1_out);
  or or_2 (or_2_out, and_6_out, and_2_out);
  or or_3 (or_3_out, and_7_out, and_3_out);
  or or_4 (C_out, and_8_out, and_4_out);
endmodule

module _4_1_MUX (
  input  I0,
  input  I1,
  input  I2,
  input  I3,
  input  S1,
  input  S0,
  output F
);

  wire and_1_out, and_2_out, and_3_out, and_4_out, not_1_out, not_2_out, or_1_out, or_2_out;

  not not_1 (not_1_out, S0);
  not not_2 (not_2_out, S1);
  and and_1 (and_1_out, I0, not_2_out, not_1_out);
  and and_2 (and_2_out, I1, not_2_out, S0);
  and and_3 (and_3_out, I2, S1, not_1_out);
  and and_4 (and_4_out, I3, S1, S0);
  or or_1 (or_1_out, and_1_out, and_2_out);
  or or_2 (or_2_out, and_3_out, and_4_out);
  or or_3 (F, or_1_out, or_2_out);
endmodule

module _8_1_MUX (
  input  I0,
  input  I1,
  input  I2,
  input  I3,
  input  I4,
  input  I5,
  input  I6,
  input  I7,
  input  S2,
  input  S1,
  input  S0,
  output Y
);

  wire n4_1_mux_1_f, n4_1_mux_2_f;

  _4_1_MUX u_4_1_mux_1 (.I0(I0), .I1(I1), .I2(I2), .I3(I3), .S1(S1), .S0(S0), .F(n4_1_mux_1_f));
  _4_1_MUX u_4_1_mux_2 (.I0(I4), .I1(I5), .I2(I6), .I3(I7), .S1(S1), .S0(S0), .F(n4_1_mux_2_f));
  Multiplexer #(.enable("false")) multiplexer_1 (.in0(n4_1_mux_1_f), .in1(n4_1_mux_2_f), .out(Y), .sel(S2));
endmodule

module _3_8_DECO (
  input  X,
  input  Y,
  input  Z,
  output D0___X_prime_Y_prime_Z_prime,
  output D1___X_prime_Y_prime_Z,
  output D2___X_prime_YZ_prime,
  output D3___X_prime_YZ,
  output D4___XY_prime_Z_prime,
  output D5___XY_prime_Z,
  output D6___XYZ_prime,
  output D7___XYZ
);

  wire not_1_out, not_2_out, not_3_out;

  not not_1 (not_1_out, X);
  not not_2 (not_2_out, Y);
  not not_3 (not_3_out, Z);
  and and_1 (D0___X_prime_Y_prime_Z_prime, not_1_out, not_2_out, not_3_out);
  and and_2 (D1___X_prime_Y_prime_Z, not_1_out, not_2_out, Z);
  and and_3 (D2___X_prime_YZ_prime, not_1_out, Y, not_3_out);
  and and_4 (D3___X_prime_YZ, not_1_out, Y, Z);
  and and_5 (D4___XY_prime_Z_prime, X, not_2_out, not_3_out);
  and and_6 (D5___XY_prime_Z, X, not_2_out, Z);
  and and_7 (D6___XYZ_prime, X, Y, not_3_out);
  and and_8 (D7___XYZ, X, Y, Z);
endmodule

module EXP1 (
  input  A,
  input  B,
  input  C,
  output F
);

  _4_1_MUX u_4_1_mux_1 (.I0(1'b1), .I1(1'b0), .I2(C), .I3(C), .S1(A), .S0(B), .F(F));
endmodule

module EXP2 (
  input  A,
  input  B,
  input  C,
  input  D,
  output F
);

  wire not_1_out;

  _8_1_MUX u_8_1_mux_1 (
    .I0(D), .I1(not_1_out), .I2(1'b1), .I3(1'b0), .I4(1'b0), .I5(not_1_out), .I6(1'b1), .I7(1'b0), .S2(A),
    .S1(B), .S0(C), .Y(F));
  not not_1 (not_1_out, D);
endmodule
